# Fritzing sketch gesture-sensor (saved by Fritzing 0.9.2b)

parts:
  Part1 = Arduino Uno (Rev3)
  Part3 = Triple Axis Accelerometer Breakout - ADXL345

nets:
  N1: Part1.A4/SDA, Part3.SCL
  N2: Part1.A5/SCL, Part3.SDA
  5V: Part1.5V, Part3.VCC
  GND: Part1.GND, Part3.GND

notes:
  A5:CL
  A4:DA
  2:DR
  **:BLK
  **:GND
